// Logisim project CPU.circ as structural Verilog: 4 circuits, main circuit main
module main (
  input  [11:0] in_1,
  input  Reset,
  output [11:0] R0,
  output [11:0] R1,
  output [11:0] R2,
  output [11:0] R4,
  output [11:0] R3,
  output [11:0] out_8,
  output [11:0] out_9,
  output [11:0] R5,
  output [11:0] out_11,
  output [11:0] R6,
  output [2:0] out_13,
  output [2:0] out_14,
  output [11:0] R7,
  output [2:0] out_16,
  output [11:0] out_17,
  output [2:0] out_18,
  output [11:0] A,
  output [11:0] B,
  output [11:0] Address,
  output [2:0] out_22,
  output [11:0] C,
  output [2:0] out_24,
  output [2:0] out_25,
  output [2:0] out_26,
  output [11:0] out_27,
  output [11:0] DataIn
);

  wire IR_Clock, Load, or_1_out, PC_Clock, RB_Clock, Store;

  Clock #(.lowDuration(3)) clock_1 (.out(PC_Clock));
  Clock clock_2 (.out(IR_Clock));
  Clock #(.highDuration(2), .lowDuration(2)) clock_3 (.out(RB_Clock));
  Decoder #(.select(3)) decoder_1 (
    .out5(Store), .out6(Load), .sel(out_9[11:9]));  // open: out0, out1, out2, out3, out4, out7, en
  or or_1 (or_1_out, Load, Store);
  Program_Counter program_counter_1 (.out_2(out_8), .in_1(PC_Clock));
  Multiplexer #(.width(12)) multiplexer_1 (.in0(out_8), .in1(B), .out(Address), .sel(or_1_out));  // open: en
  RAM #(.addrWidth(12), .dataWidth(12), .bus("separate")) ram_1 (
    .addr(Address), .din(C), .data(out_11), .str(Store), .clk(RB_Clock), .clr(Reset));  // open: sel, ld
  Register #(.width(12)) register_1 (.D(out_11), .Q(out_9), .clk(IR_Clock));  // open: en, clr
  Multiplexer #(.width(12)) multiplexer_2 (.in0(out_27), .in1(out_11), .out(out_17), .sel(Load));  // open: en
  Register_Bank register_bank_1 (
    .Rb(B), .Clock(RB_Clock), .Select_Bits_B(out_9[5:3]), .R2(R1), .R1(R0), .R3(R2), .R4(R3), .R5(R4),
    .R6(R5), .R7(R6), .R8(R7), .Rc(C), .Select_Bits_C(out_9[2:0]), .DataIn(out_17),
    .Select_Bits_A(out_9[8:6]), .Operation_Code(out_9[11:9]), .Ra(A));
  ALU alu_1 (.Register_B(B), .Register_C(C), .Output(out_27), .OPCode(out_9[11:9]));

  assign DataIn = C;
  assign out_13 = out_9[2:0];
  assign out_14 = out_9[5:3];
  assign out_16 = out_9[8:6];
  assign out_18 = out_9[11:9];
  assign out_22 = out_11[2:0];
  assign out_24 = out_11[5:3];
  assign out_25 = out_11[8:6];
  assign out_26 = out_11[11:9];

  // Other names for the same wires on the sheet: Counter[11:0] = out_8; Instruction[11:0] = out_11;
  //   IdxC[2:0] = out_9[2:0]; IdxB[2:0] = out_9[5:3]; IdxA[2:0] = out_9[8:6]; OPCode[2:0] = out_9[11:9];
  //   RegB[11:0] = B; RegC[11:0] = C

  // Notes on the sheet:
  //   Instruction Register
  //   Helen Chac & Tony Seto - SS1 Farrens 2014
  //   C
  //   B
endmodule

module Register_Bank (
  input  Clock,
  input  [11:0] DataIn,
  input  [2:0] Operation_Code,
  input  [2:0] Select_Bits_A,
  input  [2:0] Select_Bits_B,
  input  [2:0] Select_Bits_C,
  output [11:0] Ra,
  output [11:0] R1,
  output [11:0] R2,
  output [11:0] Rb,
  output [11:0] R3,
  output [11:0] R4,
  output [11:0] Rc,
  output [11:0] R5,
  output [11:0] R6,
  output [11:0] R7,
  output [11:0] R8
);

  wire Move, T0, T1, T2, T3, T4, T5, T6, T7;
  wire [11:0] multiplexer_1_out, multiplexer_2_out, multiplexer_3_out, multiplexer_4_out, multiplexer_5_out,
       multiplexer_6_out, multiplexer_7_out, multiplexer_8_out, multiplexer_9_out, or_1_out, or_2_out,
       or_3_out, or_4_out, or_5_out, or_6_out, or_7_out, or_8_out, R0, R1_t, R2_t, R3_t, R4_t, R5_t, R6_t,
       R7_t;

  assign or_1_out = R1 | {12{1'b0}};  // OR_Gate or_1, 12 bits wide
  assign or_2_out = R2 | {12{1'b0}};  // OR_Gate or_2, 12 bits wide
  assign or_3_out = R3 | {12{1'b0}};  // OR_Gate or_3, 12 bits wide
  assign or_4_out = R4 | {12{1'b0}};  // OR_Gate or_4, 12 bits wide
  assign or_5_out = R5 | {12{1'b0}};  // OR_Gate or_5, 12 bits wide
  assign or_6_out = R6 | {12{1'b0}};  // OR_Gate or_6, 12 bits wide
  assign or_7_out = R7 | {12{1'b0}};  // OR_Gate or_7, 12 bits wide
  assign or_8_out = R8 | {12{1'b0}};  // OR_Gate or_8, 12 bits wide
  Multiplexer #(.width(12)) multiplexer_1 (.in0(R0), .in1(or_1_out), .out(multiplexer_1_out), .sel(T0));  // open: en
  Multiplexer #(.width(12)) multiplexer_2 (.in0(R1_t), .in1(or_2_out), .out(multiplexer_2_out), .sel(T1));  // open: en
  Multiplexer #(.width(12)) multiplexer_3 (.in0(R2_t), .in1(or_3_out), .out(multiplexer_3_out), .sel(T2));  // open: en
  Multiplexer #(.width(12)) multiplexer_4 (.in0(R3_t), .in1(or_4_out), .out(multiplexer_4_out), .sel(T3));  // open: en
  Multiplexer #(.width(12)) multiplexer_5 (.in0(R4_t), .in1(or_5_out), .out(multiplexer_5_out), .sel(T4));  // open: en
  Multiplexer #(.width(12)) multiplexer_6 (.in0(R5_t), .in1(or_6_out), .out(multiplexer_6_out), .sel(T5));  // open: en
  Multiplexer #(.width(12)) multiplexer_7 (.in0(R6_t), .in1(or_7_out), .out(multiplexer_7_out), .sel(T6));  // open: en
  Multiplexer #(.width(12)) multiplexer_8 (.in0(R7_t), .in1(or_8_out), .out(multiplexer_8_out), .sel(T7));  // open: en
  Multiplexer #(.width(12)) multiplexer_9 (.in0(DataIn), .in1(Rb), .out(multiplexer_9_out), .sel(Move));  // open: en
  Register #(.width(12)) Register1 (.D(multiplexer_1_out), .Q(R1), .clk(Clock));  // open: en, clr
  Register #(.width(12)) Register_2 (.D(multiplexer_2_out), .Q(R2), .clk(Clock));  // open: en, clr
  Register #(.width(12)) Register_3 (.D(multiplexer_3_out), .Q(R3), .clk(Clock));  // open: en, clr
  Register #(.width(12)) Register_4 (.D(multiplexer_4_out), .Q(R4), .clk(Clock));  // open: en, clr
  Register #(.width(12)) Register_5 (.D(multiplexer_5_out), .Q(R5), .clk(Clock));  // open: en, clr
  Register #(.width(12)) Register_6 (.D(multiplexer_6_out), .Q(R6), .clk(Clock));  // open: en, clr
  Register #(.width(12)) Register_7 (.D(multiplexer_7_out), .Q(R7), .clk(Clock));  // open: en, clr
  Register #(.width(12)) Register_8 (.D(multiplexer_8_out), .Q(R8), .clk(Clock));  // open: en, clr
  Demultiplexer #(.select(3), .width(12)) demultiplexer_1 (
    .out0(R0), .out1(R1_t), .out2(R2_t), .out3(R3_t), .out4(R4_t), .out5(R5_t), .out6(R6_t), .out7(R7_t),
    .in(multiplexer_9_out), .sel(Select_Bits_A));  // open: en
  Multiplexer #(.select(3), .width(12)) multiplexer_10 (
    .in0(R1), .in1(R2), .in2(R3), .in3(R4), .in4(R5), .in5(R6), .in6(R7), .in7(R8), .out(Ra),
    .sel(Select_Bits_A));  // open: en
  Multiplexer #(.select(3), .width(12)) multiplexer_11 (
    .in0(R1), .in1(R2), .in2(R3), .in3(R4), .in4(R5), .in5(R6), .in6(R7), .in7(R8), .out(Rb),
    .sel(Select_Bits_B));  // open: en
  Multiplexer #(.select(3), .width(12)) multiplexer_12 (
    .in0(R1), .in1(R2), .in2(R3), .in3(R4), .in4(R5), .in5(R6), .in6(R7), .in7(R8), .out(Rc),
    .sel(Select_Bits_C));  // open: en
  Comparator #(.width(3)) comparator_1 (.a(3'b111), .b(Operation_Code), .eq(Move));  // open: gt, lt
  Comparator #(.width(12)) comparator_2 (.a({12{1'b0}}), .b(R0), .eq(T0));  // open: gt, lt
  Comparator #(.width(12)) comparator_3 (.a({12{1'b0}}), .b(R1_t), .eq(T1));  // open: gt, lt
  Comparator #(.width(12)) comparator_4 (.a({12{1'b0}}), .b(R2_t), .eq(T2));  // open: gt, lt
  Comparator #(.width(12)) comparator_5 (.a({12{1'b0}}), .b(R3_t), .eq(T3));  // open: gt, lt
  Comparator #(.width(12)) comparator_6 (.a({12{1'b0}}), .b(R4_t), .eq(T4));  // open: gt, lt
  Comparator #(.width(12)) comparator_7 (.a({12{1'b0}}), .b(R5_t), .eq(T5));  // open: gt, lt
  Comparator #(.width(12)) comparator_8 (.a({12{1'b0}}), .b(R6_t), .eq(T6));  // open: gt, lt
  Comparator #(.width(12)) comparator_9 (.a({12{1'b0}}), .b(R7_t), .eq(T7));  // open: gt, lt

  // Other names for the same wires on the sheet: O1[11:0] = R1; O2[11:0] = R2; O3[11:0] = R3; O4[11:0] = R4;
  //   O5[11:0] = R5; O6[11:0] = R6; O7[11:0] = R7; O8[11:0] = R8
endmodule

module ALU (
  input  [2:0] OPCode,
  input  [11:0] Register_B,
  input  [11:0] Register_C,
  output [11:0] Output
);

  wire and_1_out, and_2_out, and_3_out, and_4_out, and_5_out, and_6_out, and_7_out, and_8_out, and_9_out,
       and_10_out, and_11_out, and_12_out, c0_t, c1_t, c2_t, c3_t, c4_t, c5_t, c6_t, c7_t, c8_t, c9_t, c10_t,
       c11_t, G_2_out, G_3_out, G_4_out, G_5_out, G_6_out, G_7_out, G_8_out, G_9_out, G_10_out, G_11_out,
       G_12_out, G_out, not_1_out, not_2_out, not_3_out, not_4_out, not_5_out, not_6_out, not_7_out,
       not_8_out, not_9_out, not_10_out, not_11_out, not_12_out, or_1_out, or_2_out, or_3_out, or_4_out,
       or_5_out, or_6_out, or_7_out, or_8_out, or_9_out, or_10_out, or_11_out, or_12_out, or_13_out,
       or_14_out, or_15_out, or_16_out, or_17_out, or_18_out, or_19_out, or_20_out, or_21_out, or_22_out,
       or_23_out, or_24_out, P_2_out, P_3_out, P_out, Sub, xor_1_out, xor_2_out, xor_3_out, xor_4_out,
       xor_5_out, xor_6_out, xor_7_out, xor_8_out, xor_10_out, xor_11_out, xor_15_out, xor_16_out,
       xor_22_out, xor_23_out, xor_27_out, xor_28_out, xor_29_out, xor_30_out, xor_31_out, xor_32_out,
       xor_33_out;
  wire [1:0] multiplexer_13_out;

  and G (G_out, c11_t, Register_B[11]);
  not not_1 (not_1_out, Register_B[11]);
  Multiplexer #(.select(2)) multiplexer_1 (
    .in0(not_1_out), .in1(or_1_out), .in2(G_out), .in3(xor_2_out), .out(Output[11]), .sel(multiplexer_13_out));  // open: en
  or or_1 (or_1_out, c11_t, Register_B[11]);
  xor xor_1 (xor_1_out, c11_t, Register_B[11]);
  xor xor_2 (xor_2_out, xor_1_out, or_4_out);
  and and_1 (and_1_out, or_4_out, xor_1_out);
  or or_2 (or_2_out, G_out, and_1_out);
  and G_2 (G_2_out, c10_t, Register_B[10]);
  not not_2 (not_2_out, Register_B[10]);
  Multiplexer #(.select(2)) multiplexer_2 (
    .in0(not_2_out), .in1(or_3_out), .in2(G_2_out), .in3(xor_4_out), .out(Output[10]),
    .sel(multiplexer_13_out));  // open: en
  or or_3 (or_3_out, c10_t, Register_B[10]);
  xor xor_3 (xor_3_out, c10_t, Register_B[10]);
  xor xor_4 (xor_4_out, xor_3_out, or_6_out);
  and and_2 (and_2_out, or_6_out, xor_3_out);
  or or_4 (or_4_out, G_2_out, and_2_out);
  and G_3 (G_3_out, c9_t, Register_B[9]);
  not not_3 (not_3_out, Register_B[9]);
  or or_5 (or_5_out, c9_t, Register_B[9]);
  Multiplexer #(.select(2)) multiplexer_3 (
    .in0(not_3_out), .in1(or_5_out), .in2(G_3_out), .in3(xor_6_out), .out(Output[9]), .sel(multiplexer_13_out));  // open: en
  xor xor_5 (xor_5_out, c9_t, Register_B[9]);
  xor xor_6 (xor_6_out, xor_5_out, or_8_out);
  or or_6 (or_6_out, G_3_out, and_3_out);
  not not_4 (not_4_out, Register_B[8]);
  and and_3 (and_3_out, or_8_out, xor_5_out);
  and G_4 (G_4_out, c8_t, Register_B[8]);
  or or_7 (or_7_out, c8_t, Register_B[8]);
  Multiplexer #(.select(2)) multiplexer_4 (
    .in0(not_4_out), .in1(or_7_out), .in2(G_4_out), .in3(xor_8_out), .out(Output[8]), .sel(multiplexer_13_out));  // open: en
  xor xor_7 (xor_7_out, c8_t, Register_B[8]);
  xor xor_8 (xor_8_out, xor_7_out, or_10_out);
  and and_4 (and_4_out, or_10_out, xor_7_out);
  or or_8 (or_8_out, G_4_out, and_4_out);
  not not_5 (not_5_out, Register_B[7]);
  Comparator #(.width(3)) comparator_1 (.a(3'b100), .b(OPCode), .eq(Sub));  // open: gt, lt
  and G_5 (G_5_out, c7_t, Register_B[7]);
  or or_9 (or_9_out, c7_t, Register_B[7]);
  Multiplexer #(.select(2)) multiplexer_5 (
    .in0(not_5_out), .in1(or_9_out), .in2(G_5_out), .in3(xor_11_out), .out(Output[7]),
    .sel(multiplexer_13_out));  // open: en
  xor xor_9 (c11_t, Sub, Register_C[11]);
  xor xor_10 (xor_10_out, c7_t, Register_B[7]);
  xor xor_11 (xor_11_out, xor_10_out, or_12_out);
  and and_5 (and_5_out, or_12_out, xor_10_out);
  or or_10 (or_10_out, G_5_out, and_5_out);
  xor xor_12 (c10_t, Sub, Register_C[10]);
  and G_6 (G_6_out, c6_t, Register_B[6]);
  not not_6 (not_6_out, Register_B[6]);
  Multiplexer #(.select(2)) multiplexer_6 (
    .in0(not_6_out), .in1(or_11_out), .in2(G_6_out), .in3(xor_16_out), .out(Output[6]),
    .sel(multiplexer_13_out));  // open: en
  xor xor_13 (c9_t, Sub, Register_C[9]);
  or or_11 (or_11_out, c6_t, Register_B[6]);
  xor xor_14 (c8_t, Sub, Register_C[8]);
  xor xor_15 (xor_15_out, c6_t, Register_B[6]);
  xor xor_16 (xor_16_out, xor_15_out, or_14_out);
  xor xor_17 (c6_t, Sub, Register_C[6]);
  xor xor_18 (c7_t, Sub, Register_C[7]);
  and and_6 (and_6_out, or_14_out, xor_15_out);
  or or_12 (or_12_out, G_6_out, and_6_out);
  xor xor_19 (c5_t, Sub, Register_C[5]);
  and G_7 (G_7_out, c5_t, Register_B[5]);
  not not_7 (not_7_out, Register_B[5]);
  Multiplexer #(.select(2)) multiplexer_7 (
    .in0(not_7_out), .in1(or_13_out), .in2(G_7_out), .in3(xor_23_out), .out(Output[5]),
    .sel(multiplexer_13_out));  // open: en
  xor xor_20 (c4_t, Sub, Register_C[4]);
  or or_13 (or_13_out, c5_t, Register_B[5]);
  xor xor_21 (c3_t, Sub, Register_C[3]);
  xor xor_22 (xor_22_out, c5_t, Register_B[5]);
  xor xor_23 (xor_23_out, xor_22_out, or_16_out);
  xor xor_24 (c2_t, Sub, Register_C[2]);
  not not_8 (not_8_out, Register_B[4]);
  and and_7 (and_7_out, or_16_out, xor_22_out);
  or or_14 (or_14_out, G_7_out, and_7_out);
  xor xor_25 (c1_t, Sub, Register_C[1]);
  and G_8 (G_8_out, c4_t, Register_B[4]);
  or or_15 (or_15_out, c4_t, Register_B[4]);
  Multiplexer #(.select(2)) multiplexer_8 (
    .in0(not_8_out), .in1(or_15_out), .in2(G_8_out), .in3(xor_28_out), .out(Output[4]),
    .sel(multiplexer_13_out));  // open: en
  xor xor_26 (c0_t, Sub, Register_C[0]);
  xor xor_27 (xor_27_out, c4_t, Register_B[4]);
  xor xor_28 (xor_28_out, xor_27_out, or_18_out);
  and and_8 (and_8_out, or_18_out, xor_27_out);
  or or_16 (or_16_out, G_8_out, and_8_out);
  not not_9 (not_9_out, Register_B[3]);
  and G_9 (G_9_out, c3_t, Register_B[3]);
  or or_17 (or_17_out, c3_t, Register_B[3]);
  Multiplexer #(.select(2)) multiplexer_9 (
    .in0(not_9_out), .in1(or_17_out), .in2(G_9_out), .in3(xor_30_out), .out(Output[3]),
    .sel(multiplexer_13_out));  // open: en
  xor xor_29 (xor_29_out, c3_t, Register_B[3]);
  xor xor_30 (xor_30_out, xor_29_out, or_20_out);
  and and_9 (and_9_out, or_20_out, xor_29_out);
  or or_18 (or_18_out, G_9_out, and_9_out);
  and G_10 (G_10_out, c2_t, Register_B[2]);
  not not_10 (not_10_out, Register_B[2]);
  Multiplexer #(.select(2)) multiplexer_10 (
    .in0(not_10_out), .in1(or_19_out), .in2(G_10_out), .in3(xor_31_out), .out(Output[2]),
    .sel(multiplexer_13_out));  // open: en
  or or_19 (or_19_out, c2_t, Register_B[2]);
  xor P (P_out, c2_t, Register_B[2]);
  xor xor_31 (xor_31_out, P_out, or_22_out);
  and and_10 (and_10_out, or_22_out, P_out);
  or or_20 (or_20_out, G_10_out, and_10_out);
  and G_11 (G_11_out, c1_t, Register_B[1]);
  not not_11 (not_11_out, Register_B[1]);
  Multiplexer #(.select(2)) multiplexer_11 (
    .in0(not_11_out), .in1(or_21_out), .in2(G_11_out), .in3(xor_32_out), .out(Output[1]),
    .sel(multiplexer_13_out));  // open: en
  or or_21 (or_21_out, c1_t, Register_B[1]);
  xor P_2 (P_2_out, c1_t, Register_B[1]);
  xor xor_32 (xor_32_out, P_2_out, or_24_out);
  not not_12 (not_12_out, Register_B[0]);
  and and_11 (and_11_out, or_24_out, P_2_out);
  or or_22 (or_22_out, G_11_out, and_11_out);
  and G_12 (G_12_out, c0_t, Register_B[0]);
  or or_23 (or_23_out, c0_t, Register_B[0]);
  Multiplexer #(.select(2)) multiplexer_12 (
    .in0(not_12_out), .in1(or_23_out), .in2(G_12_out), .in3(xor_33_out), .out(Output[0]),
    .sel(multiplexer_13_out));  // open: en
  Multiplexer #(.width(2)) multiplexer_13 (
    .in0(OPCode[1:0]), .in1(2'b11), .out(multiplexer_13_out), .sel(Sub));  // open: en
  xor P_3 (P_3_out, c0_t, Register_B[0]);
  xor xor_33 (xor_33_out, P_3_out, OPCode[2]);
  and and_12 (and_12_out, OPCode[2], P_3_out);
  or or_24 (or_24_out, G_12_out, and_12_out);

  // Other names for the same wires on the sheet: Opr[2:0] = OPCode; s1 = OPCode[0]; s2 = OPCode[1]; cin = OPCode[2];
  //   o0 = Output[0]; o1 = Output[1]; o2 = Output[2]; o3 = Output[3]; o4 = Output[4]; o5 = Output[5]; o6 = Output[6];
  //   o7 = Output[7]; o8 = Output[8]; o9 = Output[9]; o10 = Output[10]; o11 = Output[11]; b0 = Register_B[0];
  //   b1 = Register_B[1]; b2 = Register_B[2]; b3 = Register_B[3]; b4 = Register_B[4]; b5 = Register_B[5];
  //   b6 = Register_B[6]; b7 = Register_B[7]; b8 = Register_B[8]; b9 = Register_B[9]; b10 = Register_B[10];
  //   b11 = Register_B[11]; C0 = Register_C[0]; C1 = Register_C[1]; C2 = Register_C[2]; C3 = Register_C[3];
  //   C4 = Register_C[4]; C5 = Register_C[5]; C6 = Register_C[6]; C7 = Register_C[7]; C8 = Register_C[8];
  //   C9 = Register_C[9]; C10 = Register_C[10]; C11 = Register_C[11]

  // Notes on the sheet:
  //   new Cin
  //   new Cin
  //   new Cin
  //   new Cin
  //   new Cin
  //   new Cin
  //   new Cin
  //   new Cin
  //   new Cin
  //   new Cin
  //   Helen Chac and Tony Seto - SS1 - Farrens 2014
  //   new Cin
endmodule

module Program_Counter (
  input  in_1,
  output [11:0] out_2
);

  wire and_1_out, and_2_out, and_3_out, and_4_out, and_5_out, and_6_out, and_7_out, and_8_out, and_9_out,
       and_10_out, and_11_out;

  and and_1 (and_1_out, 1'b1, out_2[0]);
  and and_2 (and_2_out, and_1_out, out_2[1]);
  and and_3 (and_3_out, and_2_out, out_2[2]);
  and and_4 (and_4_out, and_3_out, out_2[3]);
  J_K_Flip_Flop j_k_ff_1 (.J(1'b1), .clk(in_1), .K(1'b1), .Q(out_2[0]));  // open: Qn, preset, en, reset
  J_K_Flip_Flop j_k_ff_2 (.J(and_1_out), .clk(in_1), .K(and_1_out), .Q(out_2[1]));  // open: Qn, preset, en, reset
  J_K_Flip_Flop j_k_ff_3 (.J(and_2_out), .clk(in_1), .K(and_2_out), .Q(out_2[2]));  // open: Qn, preset, en, reset
  J_K_Flip_Flop j_k_ff_4 (.J(and_3_out), .clk(in_1), .K(and_3_out), .Q(out_2[3]));  // open: Qn, preset, en, reset
  and and_5 (and_5_out, and_4_out, out_2[4]);
  and and_6 (and_6_out, and_5_out, out_2[5]);
  and and_7 (and_7_out, and_6_out, out_2[6]);
  and and_8 (and_8_out, and_7_out, out_2[7]);
  and and_9 (and_9_out, and_8_out, out_2[8]);
  and and_10 (and_10_out, and_9_out, out_2[9]);
  and and_11 (and_11_out, and_10_out, out_2[10]);
  J_K_Flip_Flop j_k_ff_5 (.J(and_4_out), .clk(in_1), .K(and_4_out), .Q(out_2[4]));  // open: Qn, preset, en, reset
  J_K_Flip_Flop j_k_ff_6 (.J(and_5_out), .clk(in_1), .K(and_5_out), .Q(out_2[5]));  // open: Qn, preset, en, reset
  J_K_Flip_Flop j_k_ff_7 (.J(and_6_out), .clk(in_1), .K(and_6_out), .Q(out_2[6]));  // open: Qn, preset, en, reset
  J_K_Flip_Flop j_k_ff_8 (.J(and_7_out), .clk(in_1), .K(and_7_out), .Q(out_2[7]));  // open: Qn, preset, en, reset
  J_K_Flip_Flop j_k_ff_9 (.J(and_8_out), .clk(in_1), .K(and_8_out), .Q(out_2[8]));  // open: Qn, preset, en, reset
  J_K_Flip_Flop j_k_ff_10 (.J(and_9_out), .clk(in_1), .K(and_9_out), .Q(out_2[9]));  // open: Qn, preset, en, reset
  J_K_Flip_Flop j_k_ff_11 (.J(and_10_out), .clk(in_1), .K(and_10_out), .Q(out_2[10]));  // open: Qn, preset, en, reset
  J_K_Flip_Flop j_k_ff_12 (.J(and_11_out), .clk(in_1), .K(and_11_out), .Q(out_2[11]));  // open: Qn, preset, en, reset
endmodule
