// Logisim project LAB 2.3-Vending Machine.circ as structural Verilog: 1 circuit, main circuit main
module main (
  input  _11___quarter,
  input  in_2,
  output Merchandise,
  output Dime,
  output Nickel
);

  wire _1_2_out, _1_3_out, _1_4_out, _1_5_out, _1_6_out, _1_out, _2_2_out, _2_3_out, _2_4_out, _2_5_out,
       _2_6_out, _2_out, _3_2_out, _3_3_out, _3_4_out, _3_out, _4_2_out, _4_3_out, _4_out, _5_2_out, _5_out,
       clock_1_out, not_1_out, not_2_out, not_3_out, not_4_out, not_5_out, not_6_out, not_7_out, not_8_out,
       not_9_out, not_10_out, not_11_out, not_12_out, not_13_out, not_14_out, not_15_out, or_1_out, or_2_out,
       or_3_out, y1, y1b, y2, y2b, y3, y3b;

  not not_1 (not_1_out, _11___quarter);
  not not_2 (not_2_out, _11___quarter);
  not not_3 (not_3_out, in_2);
  not not_4 (not_4_out, _11___quarter);
  Clock clock_1 (.out(clock_1_out));
  not not_5 (not_5_out, in_2);
  and _4 (_4_out, y1, not_1_out, y2);
  not not_6 (not_6_out, in_2);
  not not_7 (not_7_out, _11___quarter);
  and _5 (_5_out, _11___quarter, not_3_out, y2b, y3);
  and _2 (_2_out, _11___quarter, not_5_out, y2, y1b);
  not not_8 (not_8_out, _11___quarter);
  not not_9 (not_9_out, in_2);
  and _5_2 (_5_2_out, not_2_out, in_2, y2, y3);
  and _1 (_1_out, not_6_out, y2, not_7_out);
  not not_10 (not_10_out, _11___quarter);
  and _3 (_3_out, not_4_out, in_2, y1b, y2);
  not not_11 (not_11_out, in_2);
  not not_12 (not_12_out, _11___quarter);
  not not_13 (not_13_out, _11___quarter);
  and _3_2 (_3_2_out, not_8_out, y1, not_9_out);
  and _1_2 (_1_2_out, _11___quarter, y1b, y3b, y2b, in_2);
  and _2_2 (_2_2_out, in_2, not_10_out, y3);
  not not_14 (not_14_out, in_2);
  and _3_3 (_3_3_out, not_12_out, in_2, y1b, y3b);
  not not_15 (not_15_out, in_2);
  or or_1 (or_1_out, _2_out, _3_2_out, _4_out, _5_2_out, _1_2_out);
  and _4_2 (_4_2_out, not_11_out, _11___quarter, y1b, y3b);
  and _1_3 (_1_3_out, not_14_out, y2b, y3);
  and _2_3 (_2_3_out, not_13_out, y3, not_15_out);
  or or_2 (or_2_out, _1_out, _2_2_out, _5_out, _3_out, _4_2_out);
  or or_3 (or_3_out, _1_3_out, _3_3_out, _2_3_out);
  D_Flip_Flop u_y1 (.clk(clock_1_out), .D(or_1_out), .Q(y1), .Qn(y1b));  // open: preset, en, reset
  D_Flip_Flop u_y2 (.clk(clock_1_out), .D(or_2_out), .Q(y2), .Qn(y2b));  // open: preset, en, reset
  D_Flip_Flop u_y3 (.clk(clock_1_out), .D(or_3_out), .Q(y3), .Qn(y3b));  // open: preset, en, reset
  and _2_4 (_2_4_out, _11___quarter, y1);
  and _3_4 (_3_4_out, _11___quarter, in_2, y3);
  and _4_3 (_4_3_out, _11___quarter, in_2, y2);
  and _1_4 (_1_4_out, in_2, y1, y2b);
  and _1_5 (_1_5_out, _11___quarter, in_2, y1);
  and _2_5 (_2_5_out, _11___quarter, in_2, y2, y3);
  and _2_6 (_2_6_out, _11___quarter, in_2, y2, y3b);
  and _1_6 (_1_6_out, _11___quarter, y1, y2b);
  or or_4 (Merchandise, _2_4_out, _3_4_out, _4_3_out, _1_4_out);
  or or_5 (Dime, _1_5_out, _2_5_out);
  or or_6 (Nickel, _2_6_out, _1_6_out);

  // Other names for the same wires on the sheet: x1 = _11___quarter; x2 = in_2

  // Notes on the sheet:
  //   10 - dime
  //   01 - nickel
  //   00 - nothing
endmodule
