// Logisim project LAB2-1 - Combinational.circ as structural Verilog: 1 circuit, main circuit main
module main (
  input  in_1,
  output Z
);

  wire and_1_out, and_2_out, and_3_out, and_4_out, and_5_out, and_6_out, and_7_out, and_8_out, and_9_out,
       clock_1_out, not_1_out, not_2_out, not_3_out, not_4_out, or_1_out, or_2_out, or_3_out, y1, y1b, y2,
       y2b, y3, y3b;

  Clock clock_1 (.out(clock_1_out));
  not not_1 (not_1_out, in_1);
  not not_2 (not_2_out, in_1);
  not not_3 (not_3_out, in_1);
  and and_1 (and_1_out, in_1, y1b, y3);
  and and_2 (and_2_out, y1, y2b, y3);
  and and_3 (and_3_out, not_1_out, y2, y1b);
  or or_1 (or_1_out, and_1_out, and_2_out, and_3_out);
  and and_4 (and_4_out, in_1, y1b, y3b);
  and and_5 (and_5_out, y1, y3, y2b);
  and and_6 (and_6_out, not_2_out, y1b, y3);
  and and_7 (and_7_out, y2b, y3);
  and and_8 (and_8_out, y2, y3b);
  and and_9 (and_9_out, not_3_out, y1b);
  or or_2 (or_2_out, and_4_out, and_5_out, and_6_out);
  or or_3 (or_3_out, and_7_out, and_8_out, and_9_out);
  D_Flip_Flop u_y1 (.clk(clock_1_out), .D(or_1_out), .Q(y1), .Qn(y1b));  // open: preset, en, reset
  D_Flip_Flop u_y2 (.clk(clock_1_out), .D(or_2_out), .Q(y2), .Qn(y2b));  // open: preset, en, reset
  D_Flip_Flop u_y3 (.clk(clock_1_out), .D(or_3_out), .Q(y3), .Qn(y3b));  // open: preset, en, reset
  not not_4 (not_4_out, in_1);
  and and_10 (Z, not_4_out, y1, y3b);

  // Other names for the same wires on the sheet: W = in_1

  // Notes on the sheet:
  //   Helen Chac & Tony Seto- Farrens 2014 - SS 1
endmodule
