// Logisim project Lab 1.1.circ as structural Verilog: 1 circuit, main circuit main
module main (
  input  A,
  input  B,
  input  C,
  output out_4
);

  wire and_1_out, and_2_out, and_3_out;

  and and_1 (and_1_out, C, A, A);
  and and_2 (and_2_out, A, B);
  and and_3 (and_3_out, B, C);
  or or_1 (out_4, and_1_out, and_2_out, and_3_out);

  // Notes on the sheet:
  //   Helen Chac& Tony Seto ECS 154a - SS!, 2014
endmodule
