// Logisim project SEC.circ as structural Verilog: 1 circuit, main circuit main
module main (
  input  _12,
  input  _11,
  input  _10,
  input  _9,
  input  _8,
  input  _7,
  input  _6,
  input  _5,
  input  _4,
  input  _3,
  input  _2,
  input  _1,
  output Output,
  output out_14,
  output out_15,
  output out_16,
  output out_17,
  output out_18,
  output out_19,
  output out_20
);

  wire c0_prime, c1_prime, c2_prime, c3_prime, d0_prime, d1_prime, d2_prime, d3_prime, d4_prime, d5_prime,
       d6_prime, d7_prime, xor_1_out, xor_2_out, xor_3_out, xor_4_out, xor_5_out, xor_6_out, xor_7_out,
       xor_8_out, xor_9_out, xor_10_out;
  wire [3:0] xor_18_out;

  xor xor_1 (xor_1_out, _3, _5);
  xor xor_2 (xor_2_out, _3, _6);
  xor xor_3 (xor_3_out, _5, _6);
  xor xor_4 (xor_4_out, _9, _10);
  xor xor_5 (xor_5_out, xor_1_out, _7);
  xor xor_6 (xor_6_out, xor_2_out, _7);
  xor xor_7 (xor_7_out, xor_3_out, _7);
  xor xor_8 (xor_8_out, xor_4_out, _11);
  xor xor_9 (xor_9_out, xor_5_out, _9);
  xor xor_10 (xor_10_out, xor_6_out, _10);
  xor xor_11 (c2_prime, xor_7_out, _12);
  xor xor_12 (c3_prime, xor_8_out, _12);
  xor xor_13 (c0_prime, xor_9_out, _11);
  xor xor_14 (c1_prime, xor_10_out, _11);
  Decoder #(.select(4)) decoder_1 (
    .out3(d0_prime), .out5(d1_prime), .out6(d2_prime), .out7(d3_prime), .out9(d4_prime), .out10(d5_prime),
    .out11(d6_prime), .out12(d7_prime), .sel(xor_18_out));  // open: out0, out1, out2, out4, out8, out13, out14, out15, en
  xor xor_15 (xor_18_out[3], _8, c3_prime);
  xor xor_16 (xor_18_out[2], _4, c2_prime);
  xor xor_17 (xor_18_out[1], _2, c1_prime);
  xor xor_18 (xor_18_out[0], _1, c0_prime);
  xor xor_19 (out_20, _3, d0_prime);
  xor xor_20 (out_19, _5, d1_prime);
  xor xor_21 (out_18, _6, d2_prime);
  xor xor_22 (out_17, _7, d3_prime);
  xor xor_23 (out_16, _9, d4_prime);
  xor xor_24 (out_15, _10, d5_prime);
  xor xor_25 (out_14, _11, d6_prime);
  xor xor_26 (Output, _12, d7_prime);

  // Other names for the same wires on the sheet: c0 = _1; c1 = _2; c2 = _4; c3 = _8; d0 = _3; d1 = _5; d2 = _6;
  //   d3 = _7; d4 = _9; d5 = _10; d6 = _11; d7 = _12; z0 = out_20; z1 = out_19; z2 = out_18; z3 = out_17; z4 = out_16;
  //   z5 = out_15; z6 = out_14; z7 = Output

  // Notes on the sheet:
  //   XOR to find your new c0, c1, c2, c3
  //   Helen Chac & Tony Seto - Farrens, Summer Session 1 2014
  //   XOR the two c values to get the position that changed
endmodule
