// Logisim project lab 1.2.circ as structural Verilog: 1 circuit, main circuit main
module main (
  input  A,
  input  B,
  input  Cin,
  input  D,
  input  E,
  output MSB,
  output out_7,
  output LSB
);

  wire AB_out, and_1_out, and_2_out, and_3_out, AND_4_out, and_5_out, AXORB_out, or_1_out, xor_1_out,
       xor_2_out, xor_3_out, xor_4_out, xor_6_out;

  and and_1 (and_1_out, Cin, xor_1_out);
  xor xor_1 (xor_1_out, B, A);
  and and_2 (and_2_out, B, A);
  xor xor_2 (xor_2_out, Cin, A);
  and and_3 (and_3_out, D, E);
  xor xor_3 (xor_3_out, E, D);
  or or_1 (or_1_out, and_1_out, and_2_out);
  xor xor_4 (xor_4_out, xor_2_out, B);
  and AND_4 (AND_4_out, xor_4_out, xor_3_out);
  xor xor_5 (LSB, xor_4_out, xor_3_out);
  xor xor_6 (xor_6_out, and_3_out, AND_4_out);
  and AB (AB_out, or_1_out, AND_4_out);
  xor xor_7 (out_7, or_1_out, xor_6_out);
  xor AXORB (AXORB_out, or_1_out, AND_4_out);
  and and_5 (and_5_out, AXORB_out, and_3_out);
  or or_2 (MSB, AB_out, and_5_out);

  // Notes on the sheet:
  //   Cout
  //   Sum
  //   Carry
  //   Sum
  //   Tony Seto & Helen Chac - SS1 2014, Farrens, ECS 154A
endmodule
