// Logisim project lab 1.4.circ as structural Verilog: 1 circuit, main circuit main
module main (
  input  b3,
  input  a3,
  input  b2,
  input  a2,
  input  b1,
  input  a1,
  input  b0,
  input  a0,
  input  cin,
  input  s0,
  input  s1,
  output out_12,
  output c3,
  output c2,
  output c1,
  output c0
);

  wire and_1_out, and_2_out, and_3_out, and_4_out, G_2_out, G_3_out, G_4_out, G_out, not_1_out, not_2_out,
       not_3_out, not_4_out, or_1_out, or_3_out, or_4_out, or_5_out, or_6_out, or_7_out, or_8_out, P_2_out,
       P_3_out, P_out, xor_1_out, xor_2_out, xor_3_out, xor_4_out, xor_5_out;

  not not_1 (not_1_out, a3);
  and G (G_out, b3, a3);
  or or_1 (or_1_out, b3, a3);
  Multiplexer #(.select(2)) multiplexer_1 (
    .in0(not_1_out), .in1(or_1_out), .in2(G_out), .in3(xor_2_out), .out(c3), .sel({s1, s0}));  // open: en
  xor xor_1 (xor_1_out, b3, a3);
  xor xor_2 (xor_2_out, xor_1_out, or_4_out);
  and and_1 (and_1_out, or_4_out, xor_1_out);
  or or_2 (out_12, G_out, and_1_out);
  and G_2 (G_2_out, b2, a2);
  not not_2 (not_2_out, a2);
  Multiplexer #(.select(2)) multiplexer_2 (
    .in0(not_2_out), .in1(or_3_out), .in2(G_2_out), .in3(xor_3_out), .out(c2), .sel({s1, s0}));  // open: en
  or or_3 (or_3_out, b2, a2);
  xor P (P_out, b2, a2);
  xor xor_3 (xor_3_out, P_out, or_6_out);
  and and_2 (and_2_out, or_6_out, P_out);
  or or_4 (or_4_out, G_2_out, and_2_out);
  and G_3 (G_3_out, b1, a1);
  not not_3 (not_3_out, a1);
  Multiplexer #(.select(2)) multiplexer_3 (
    .in0(not_3_out), .in1(or_5_out), .in2(G_3_out), .in3(xor_4_out), .out(c1), .sel({s1, s0}));  // open: en
  or or_5 (or_5_out, b1, a1);
  xor P_2 (P_2_out, b1, a1);
  xor xor_4 (xor_4_out, P_2_out, or_8_out);
  not not_4 (not_4_out, a0);
  and and_3 (and_3_out, or_8_out, P_2_out);
  or or_6 (or_6_out, G_3_out, and_3_out);
  and G_4 (G_4_out, b0, a0);
  or or_7 (or_7_out, b0, a0);
  Multiplexer #(.select(2)) multiplexer_4 (
    .in0(not_4_out), .in1(or_7_out), .in2(G_4_out), .in3(xor_5_out), .out(c0), .sel({s1, s0}));  // open: en
  xor P_3 (P_3_out, b0, a0);
  xor xor_5 (xor_5_out, P_3_out, cin);
  and and_4 (and_4_out, cin, P_3_out);
  or or_8 (or_8_out, G_4_out, and_4_out);

  // Notes on the sheet:
  //   new Cin
  //   new Cin
  //   Helen Chac and Tony Seto - SS1 - Farrens 2014
  //   new Cin
endmodule
