// Logisim project lab1.3.circ as structural Verilog: 1 circuit, main circuit main
module main (
  input  w0,
  input  w1,
  input  w2,
  input  w3,
  output out_5,
  output out_6,
  output out_7,
  output out_8,
  output out_9,
  output out_10,
  output out_11
);

  wire and_1_out, and_2_out, and_3_out, and_4_out, and_5_out, and_6_out, and_7_out, and_8_out, and_9_out,
       and_10_out, and_11_out, and_12_out, not_1_out, not_2_out, not_3_out, not_4_out;

  not not_1 (not_1_out, w0);
  not not_2 (not_2_out, w1);
  not not_3 (not_3_out, w2);
  not not_4 (not_4_out, w3);
  and and_1 (and_1_out, w1, not_1_out);
  and and_2 (and_2_out, w2, not_4_out);
  and and_3 (and_3_out, not_4_out, not_3_out);
  and and_4 (and_4_out, w1, w0);
  and and_5 (and_5_out, w2, not_2_out);
  and and_6 (and_6_out, not_2_out, not_1_out, not_3_out);
  and and_7 (and_7_out, not_1_out, not_2_out);
  and and_8 (and_8_out, and_5_out, w0);
  and and_9 (and_9_out, w0, and_2_out);
  and and_10 (and_10_out, w1, w0);
  and and_11 (and_11_out, and_3_out, w1, w1);
  and and_12 (and_12_out, and_1_out, w2);
  or A (out_5, w3, and_9_out, w1, and_6_out);
  or B (out_6, w3, and_3_out, and_7_out, and_4_out);
  or C (out_7, w3, not_2_out, and_2_out, and_10_out);
  or D (out_8, w3, and_1_out, and_6_out, and_11_out, and_8_out);
  or E (out_9, and_1_out, and_6_out);
  or F (out_10, and_7_out, w3, and_5_out, and_12_out);
  or G (out_11, and_1_out, w3, and_5_out, and_11_out);
  _7_Segment_Display u_7_segment_display_1 (
    .g(out_11), .f(out_10), .a(out_5), .b(out_6), .e(out_9), .d(out_8), .c(out_7));  // open: dp

  // Notes on the sheet:
  //   Tony Seto and Helen Chac - ECS 154A Farrens, SS1 2014
endmodule
