// Logisim project lab2.1.circ as structural Verilog: 2 circuits, main circuit main
module main (
  input  in_1,
  output Z
);

  wire and_1_out, and_2_out, and_3_out, and_4_out, and_5_out, and_6_out, and_7_out, and_8_out, clock_1_out,
       not_1_out, not_2_out, or_1_out, y1, y1b, y2, y2b, y3, y3b;

  Clock clock_1 (.out(clock_1_out));
  and and_1 (and_1_out, in_1, y1b);
  and and_2 (and_2_out, in_1, y1b, y2, y3b);
  and and_3 (and_3_out, y1b, y2, y3b);
  and and_4 (and_4_out, in_1, y2b);
  and and_5 (and_5_out, in_1, y2, y3b);
  not not_1 (not_1_out, in_1);
  or or_1 (or_1_out, and_3_out, and_4_out, and_1_out, and_5_out);
  and and_6 (and_6_out, not_1_out, y1b, y2, y3b);
  D_Flip_Flop u_y1 (.clk(clock_1_out), .D(and_2_out), .Q(y1), .Qn(y1b));  // open: preset, en, reset
  D_Flip_Flop u_y2 (.clk(clock_1_out), .D(or_1_out), .Q(y2), .Qn(y2b));  // open: preset, en, reset
  D_Flip_Flop u_y3 (.clk(clock_1_out), .D(and_6_out), .Q(y3), .Qn(y3b));  // open: preset, en, reset
  not not_2 (not_2_out, in_1);
  and and_7 (and_7_out, in_1, y1, y2b, y3b);
  and and_8 (and_8_out, not_2_out, y1b, y3);
  or or_2 (Z, and_7_out, and_8_out);

  // Other names for the same wires on the sheet: W = in_1

  // Notes on the sheet:
  //   Helen Chac & Tony Seto- Farrens 2014 - SS 1
endmodule

module save (
);

  wire and_1_out, and_2_out, and_3_out, and_4_out, and_5_out, and_6_out, and_7_out, and_8_out, and_9_out,
       and_10_out, not_1_out, not_2_out, W, y1, y1b, y2, y2b, y3, y3b;

  and and_1 (and_1_out, y1, y2b, y3);
  and and_2 (and_2_out, W, y1b, y3);
  and and_3 (and_3_out, y1b, y2, y3);
  and and_4 (and_4_out, W, y1, y2b, y3);
  not not_1 (not_1_out, W);
  and and_5 (and_5_out, W, y1b, y3b);
  not not_2 (not_2_out, W);
  and and_6 (and_6_out, not_1_out, y1b, y3);
  and and_7 (and_7_out, y1b, y2);
  and and_8 (and_8_out, not_2_out, y1);
  and and_9 (and_9_out, y1b, y3);
  and and_10 (and_10_out, y1b, y2);
  // OR_Gate or_1 has open pins: in0=and_1_out, in1=and_2_out, in2=and_3_out, out=open
  // OR_Gate or_2 has open pins: in0=and_4_out, in1=and_6_out, in2=and_5_out, in3=and_7_out, out=open
  // OR_Gate or_3 has open pins: in0=and_8_out, in1=and_9_out, in2=and_10_out, out=open
endmodule
